// Logisim project 10234_ass3.circ as structural Verilog
module HALF_ADDER (
  input  A,
  input  B,
  input  C,
  output S,
  output C_2
);

  wire and_1_out, and_2_out, and_3_out, and_4_out, and_5_out, and_6_out, and_7_out, and_8_out, and_9_out,
       and_10_out, and_11_out, not_1_out, not_2_out, not_3_out, not_4_out, not_5_out, not_6_out, or_1_out,
       or_3_out, or_4_out;

  not not_1 (not_1_out, A);
  not not_2 (not_2_out, B);
  not not_3 (not_3_out, A);
  not not_4 (not_4_out, B);
  and and_1 (and_1_out, B, C);
  and and_2 (and_2_out, A, C);
  and and_3 (and_3_out, not_1_out, not_2_out);
  and and_4 (and_4_out, not_3_out, B);
  not not_5 (not_5_out, C);
  and and_5 (and_5_out, A, not_4_out);
  not not_6 (not_6_out, C);
  and and_6 (and_6_out, A, B);
  or or_1 (or_1_out, and_1_out, and_2_out);
  and and_7 (and_7_out, A, B);
  and and_8 (and_8_out, and_3_out, C);
  and and_9 (and_9_out, and_4_out, not_5_out);
  and and_10 (and_10_out, and_5_out, not_6_out);
  and and_11 (and_11_out, and_6_out, C);
  or or_2 (C_2, or_1_out, and_7_out);
  or or_3 (or_3_out, and_8_out, and_9_out);
  or or_4 (or_4_out, and_10_out, and_11_out);
  or or_5 (S, or_3_out, or_4_out);
endmodule

module FULL_ADDER (
  input  in_1,
  input  [3:0] in_2,
  input  [3:0] in_3,
  output [3:0] out_4,
  output out_5
);

  wire half_adder_1_c_2, half_adder_2_c_2, half_adder_3_c_2;

  HALF_ADDER half_adder_1 (.A(in_1), .B(in_2[0]), .C(in_3[0]), .S(out_4[0]), .C_2(half_adder_1_c_2));
  HALF_ADDER half_adder_2 (.A(half_adder_1_c_2), .B(in_2[1]), .C(in_3[1]), .S(out_4[1]), .C_2(half_adder_2_c_2));
  HALF_ADDER half_adder_3 (.A(half_adder_2_c_2), .B(in_2[2]), .C(in_3[2]), .S(out_4[2]), .C_2(half_adder_3_c_2));
  HALF_ADDER half_adder_4 (.A(half_adder_3_c_2), .B(in_2[3]), .C(in_3[3]), .S(out_4[3]), .C_2(out_5));
endmodule

module BCD_ADDER (
  input  in_1,
  input  Cin,
  input  in_3,
  input  [3:0] A,
  input  [3:0] B,
  output [3:0] OUTPUT,
  output Cout
);

  wire and_1_out, and_2_out, full_adder_1_out_5;
  wire [3:0] full_adder_1_out_4;

  FULL_ADDER full_adder_1 (.in_1(Cin), .in_2(A), .in_3(B), .out_4(full_adder_1_out_4), .out_5(full_adder_1_out_5));
  FULL_ADDER full_adder_2 (
    .in_1(in_3), .in_2(full_adder_1_out_4), .in_3({in_1, {2{Cout}}, in_1}), .out_4(OUTPUT));  // open: out_5
  and and_1 (and_1_out, full_adder_1_out_4[1], full_adder_1_out_4[3]);
  and and_2 (and_2_out, full_adder_1_out_4[2], full_adder_1_out_4[3]);
  or or_1 (Cout, and_1_out, and_2_out, full_adder_1_out_5);
endmodule
