// Logisim project 10234_ass4.circ as structural Verilog
module MASTER_SLAVE_D_FLIP_FLOP (
  input  DATA,
  output Q
);

  wire clock_1_out, Master_q, not_1_out;

  Clock clock_1 (.out(clock_1_out));
  not not_1 (not_1_out, clock_1_out);
  d_latch Master (.D(DATA), .in_2(clock_1_out), .Q(Master_q));  // open: Q_prime
  d_latch Slave (.D(Master_q), .in_2(not_1_out), .Q(Q));  // open: Q_prime

  // Notes on the sheet:
  //   CLOCK
  //   MASTER SLAVE D FLIP FLOP
endmodule

module FOUR_BIT_MEMORY_USING_D_FF (
  input  D0,
  input  D1,
  input  D2,
  input  D3,
  output Q0,
  output Q1,
  output Q3,
  output Q4
);

  wire clock_1_out;

  Clock clock_1 (.out(clock_1_out));
  d_latch d_latch_1 (.D(D0), .in_2(clock_1_out), .Q(Q0));  // open: Q_prime
  d_latch d_latch_2 (.D(D1), .in_2(clock_1_out), .Q(Q1));  // open: Q_prime
  d_latch d_latch_3 (.D(D2), .in_2(clock_1_out), .Q(Q3));  // open: Q_prime
  d_latch d_latch_4 (.D(D3), .in_2(clock_1_out), .Q(Q4));  // open: Q_prime

  // Notes on the sheet:
  //   CLOCK
  //   4-BIT MEMORY USING D FLIP FLOP
endmodule

module FOUR_BIT_SHIFT_REGISTER (
  input  in_1,
  output Q1,
  output Q2,
  output Q0,
  output Q3
);

  wire clock_1_out;

  Clock clock_1 (.out(clock_1_out));
  d_latch d_latch_1 (.D(in_1), .in_2(clock_1_out), .Q(Q0));  // open: Q_prime
  d_latch d_latch_2 (.D(Q0), .in_2(clock_1_out), .Q(Q1));  // open: Q_prime
  d_latch d_latch_3 (.D(Q1), .in_2(clock_1_out), .Q(Q2));  // open: Q_prime
  d_latch d_latch_4 (.D(Q2), .in_2(clock_1_out), .Q(Q3));  // open: Q_prime

  // Notes on the sheet:
  //   Clock
  //   serial data input
  //   4-BIT SHIFT REGISTER
endmodule

module FREQUENCY_DIVIDER_USING_D_FF (
  input  F0,
  output out_2
);

  wire d_ff_1_qn;

  D_Flip_Flop d_ff_1 (.D(d_ff_1_qn), .clk(F0), .Q(out_2), .Qn(d_ff_1_qn));  // open: preset, reset

  // Notes on the sheet:
  //   Frequency divider
  //   Feedback loop
  //   F0/2
endmodule

module d_latch (
  input  D,
  input  in_2,
  output Q,
  output Q_prime
);

  wire and_1_out, and_2_out, not_1_out;

  not not_1 (not_1_out, D);
  and and_1 (and_1_out, D, in_2);
  and and_2 (and_2_out, in_2, not_1_out);
  nor nor_1 (Q, and_1_out, Q_prime);
  nor nor_2 (Q_prime, Q, and_2_out);
endmodule
