// Logisim project SR_flip_flop.circ as structural Verilog: 1 circuit, main circuit main
module main (
  input  S,
  input  R,
  input  PRESET,
  input  ENABLE,
  input  CLEAR,
  output Q,
  output nQ
);

  wire CLOCK_out;

  Clock CLOCK (.out(CLOCK_out));
  S_R_Flip_Flop s_r_ff_1 (.S(S), .clk(CLOCK_out), .R(R), .Q(Q), .Qn(nQ), .preset(PRESET), .reset(CLEAR), .en(ENABLE));
endmodule
