// Logisim project lab07.circ as structural Verilog: 6 circuits, main circuit SR Latch
module SR_Latch (
  input  R,
  input  S,
  output Q_t,
  output Q_t__prime
);

  nor nor_1 (Q_t, R, Q_t__prime);
  nor nor_2 (Q_t__prime, Q_t, S);

  // Notes on the sheet:
  //   SR Latch
endmodule

module Gated_SR_Latch (
  input  R,
  input  E,
  input  S,
  output Q_t,
  output Q_t__prime
);

  wire and_1_out, and_2_out;

  and and_1 (and_1_out, R, E);
  and and_2 (and_2_out, E, S);
  nor nor_1 (Q_t, and_1_out, Q_t__prime);
  nor nor_2 (Q_t__prime, Q_t, and_2_out);

  // Notes on the sheet:
  //   Gated SR Latch
endmodule

module D_Latch (
  input  E,
  input  D,
  output Q_t,
  output Q_t__prime
);

  wire and_1_out, and_2_out, not_1_out;

  not not_1 (not_1_out, D);
  and and_1 (and_1_out, not_1_out, E);
  and and_2 (and_2_out, E, D);
  nor nor_1 (Q_t, and_1_out, Q_t__prime);
  nor nor_2 (Q_t__prime, Q_t, and_2_out);
endmodule

module SR_Flipflop (
  input  R,
  input  S,
  output Q_t,
  output Q_t__prime
);

  wire and_1_out, and_2_out, clock_1_out;

  Clock clock_1 (.out(clock_1_out));
  and and_1 (and_1_out, R, clock_1_out);
  and and_2 (and_2_out, clock_1_out, S);
  nor nor_1 (Q_t, and_1_out, Q_t__prime);
  nor nor_2 (Q_t__prime, Q_t, and_2_out);

  // Notes on the sheet:
  //   SR Flipflop
endmodule

module D_flipflop (
  input  D,
  output Q_t,
  output Q_t__prime
);

  wire and_1_out, and_2_out, clock_1_out, not_1_out;

  not not_1 (not_1_out, D);
  Clock clock_1 (.out(clock_1_out));
  and and_1 (and_1_out, not_1_out, clock_1_out);
  and and_2 (and_2_out, clock_1_out, D);
  nor nor_1 (Q_t, and_1_out, Q_t__prime);
  nor nor_2 (Q_t__prime, Q_t, and_2_out);
endmodule

module K_Flipflop (
  input  K,
  input  J,
  output Q_t,
  output Q_t__prime
);

  wire and_1_out, and_2_out, CLK_out;

  Clock CLK (.out(CLK_out));
  and and_1 (and_1_out, Q_t, K, CLK_out);
  and and_2 (and_2_out, CLK_out, J, Q_t__prime);
  nor nor_1 (Q_t, and_1_out, Q_t__prime);
  nor nor_2 (Q_t__prime, Q_t, and_2_out);
endmodule
