// Logisim project adders.circ as structural Verilog
module FULL_ADDER (
  input  A,
  input  B,
  input  C,
  output Sum,
  output Carry
);

  wire and_1_out, and_2_out, and_3_out, and_4_out, and_5_out, and_6_out, and_7_out, not_1_out, not_2_out,
       not_3_out, not_4_out, not_5_out, not_6_out;

  not not_1 (not_1_out, A);
  not not_2 (not_2_out, B);
  not not_3 (not_3_out, A);
  not not_4 (not_4_out, C);
  not not_5 (not_5_out, B);
  not not_6 (not_6_out, C);
  and and_1 (and_1_out, B, C);
  and and_2 (and_2_out, A, C);
  and and_3 (and_3_out, A, B);
  and and_4 (and_4_out, not_1_out, not_2_out, C);
  and and_5 (and_5_out, not_3_out, B, not_4_out);
  and and_6 (and_6_out, A, not_5_out, not_6_out);
  and and_7 (and_7_out, A, B, C);
  or or_1 (Carry, and_1_out, and_2_out, and_3_out);
  or or_2 (Sum, and_4_out, and_5_out, and_6_out, and_7_out);
endmodule

module _4_bit_full_adder (
  input  Previous_carry,
  input  [3:0] in_2,
  input  [3:0] in_3,
  output [3:0] out_4,
  output Carry_out
);

  wire full_adder_1_carry, full_adder_2_carry, full_adder_3_carry;

  FULL_ADDER full_adder_1 (.A(Previous_carry), .B(in_2[0]), .C(in_2[0]), .Sum(out_4[0]), .Carry(full_adder_1_carry));
  FULL_ADDER full_adder_2 (
    .A(full_adder_1_carry), .B(in_2[1]), .C(in_3[1]), .Sum(out_4[1]), .Carry(full_adder_2_carry));
  FULL_ADDER full_adder_3 (
    .A(full_adder_2_carry), .B(in_2[2]), .C(in_3[2]), .Sum(out_4[2]), .Carry(full_adder_3_carry));
  FULL_ADDER full_adder_4 (.A(full_adder_3_carry), .B(in_2[3]), .C(in_3[3]), .Sum(out_4[3]), .Carry(Carry_out));

  assign in_3[0] = in_2[0];

  // Notes on the sheet:
  //   FULL ADDER : 4 BIT ADDER
  //   A
  //   B
  //   C
  //   D
endmodule

module _8_bit_full_adder (
  input  in_1,
  input  [7:0] in_2,
  input  [7:0] in_3,
  output [7:0] out_4,
  output out_5
);

  wire n4_bit_full_adder_1_carry_out;

  _4_bit_full_adder u_4_bit_full_adder_1 (
    .Previous_carry(in_1), .in_2(in_2[3:0]), .in_3(in_3[3:0]), .out_4(out_4[3:0]),
    .Carry_out(n4_bit_full_adder_1_carry_out));
  _4_bit_full_adder u_4_bit_full_adder_2 (
    .Previous_carry(n4_bit_full_adder_1_carry_out), .in_2(in_2[7:4]), .in_3(in_3[7:4]), .out_4(out_4[7:4]),
    .Carry_out(out_5));
endmodule

module _16_bit_full_adder (
  input  in_1,
  input  [15:0] in_2,
  input  [15:0] in_3,
  output [15:0] out_4,
  output out_5
);

  wire n8_bit_full_adder_1_out_5;

  _8_bit_full_adder u_8_bit_full_adder_1 (
    .in_1(in_1), .in_2(in_2[7:0]), .in_3(in_3[7:0]), .out_4(out_4[7:0]), .out_5(n8_bit_full_adder_1_out_5));
  _8_bit_full_adder u_8_bit_full_adder_2 (
    .in_1(n8_bit_full_adder_1_out_5), .in_2(in_2[15:8]), .in_3(in_3[15:8]), .out_4(out_4[15:8]), .out_5(out_5));
endmodule

module FULL_SUBTRACTOR (
  input  A,
  input  B,
  input  C,
  output Diff,
  output Borrow
);

  wire and_1_out, and_2_out, and_3_out, and_4_out, and_5_out, and_6_out, and_7_out, not_1_out, not_2_out,
       not_3_out, not_4_out, not_5_out, not_6_out, not_7_out, not_8_out;

  not not_1 (not_1_out, A);
  not not_2 (not_2_out, B);
  not not_3 (not_3_out, A);
  not not_4 (not_4_out, C);
  not not_5 (not_5_out, B);
  not not_6 (not_6_out, C);
  not not_7 (not_7_out, A);
  not not_8 (not_8_out, A);
  and and_1 (and_1_out, not_1_out, not_2_out, C);
  and and_2 (and_2_out, not_3_out, B, not_4_out);
  and and_3 (and_3_out, A, not_5_out, not_6_out);
  and and_4 (and_4_out, A, B, C);
  and and_5 (and_5_out, not_7_out, C);
  or or_1 (Borrow, and_5_out, and_6_out, and_7_out);
  and and_6 (and_6_out, not_8_out, B);
  and and_7 (and_7_out, B, C);
  or or_2 (Diff, and_1_out, and_2_out, and_3_out, and_4_out);
endmodule

module _4_bit_full_subtractor (
  input  Previous_borrow,
  input  [3:0] in_2,
  input  [3:0] in_3,
  output [3:0] out_4,
  output Borrow_out
);

  wire full_subtractor_1_borrow, full_subtractor_2_borrow, full_subtractor_3_borrow;

  FULL_SUBTRACTOR full_subtractor_1 (
    .A(Previous_borrow), .B(in_2[0]), .C(in_3[0]), .Diff(out_4[0]), .Borrow(full_subtractor_1_borrow));
  FULL_SUBTRACTOR full_subtractor_2 (
    .A(full_subtractor_1_borrow), .B(in_2[1]), .C(in_3[1]), .Diff(out_4[1]), .Borrow(full_subtractor_2_borrow));
  FULL_SUBTRACTOR full_subtractor_3 (
    .A(full_subtractor_2_borrow), .B(in_2[2]), .C(in_3[2]), .Diff(out_4[2]), .Borrow(full_subtractor_3_borrow));
  FULL_SUBTRACTOR full_subtractor_4 (
    .A(full_subtractor_3_borrow), .B(in_2[3]), .C(in_3[3]), .Diff(out_4[3]), .Borrow(Borrow_out));

  // Notes on the sheet:
  //   FULL SUBTRACTOR : 4 BIT SUBTRACTOR
  //   A
  //   B
  //   C
  //   D
endmodule

module _8_bit_full_subtractor (
  input  in_1,
  input  [7:0] in_2,
  input  [7:0] in_3,
  output [7:0] out_4,
  output out_5
);

  wire n4_bit_full_subtractor_1_borrow_out;

  _4_bit_full_subtractor u_4_bit_full_subtractor_1 (
    .Previous_borrow(in_1), .in_2(in_2[3:0]), .in_3(in_3[3:0]), .out_4(out_4[3:0]),
    .Borrow_out(n4_bit_full_subtractor_1_borrow_out));
  _4_bit_full_subtractor u_4_bit_full_subtractor_2 (
    .Previous_borrow(n4_bit_full_subtractor_1_borrow_out), .in_2(in_2[7:4]), .in_3(in_3[7:4]),
    .out_4(out_4[7:4]), .Borrow_out(out_5));
endmodule

module ADDER_AND_SUBTRACTOR_IN_SAME_CIRCUIT (
  input  B0,
  input  A0,
  input  B1,
  input  A1,
  input  B2,
  input  A2,
  input  B3,
  input  A3,
  input  Control,
  output out_10,
  output out_11,
  output out_12,
  output out_13,
  output out_14
);

  wire full_adder_1_carry, full_adder_2_carry, full_adder_3_carry, xor_1_out, xor_2_out, xor_3_out;

  xor xor_1 (xor_1_out, B0, Control);
  xor xor_2 (xor_2_out, B1, Control);
  xor xor_3 (xor_3_out, B2, Control);
  xor xor_4 (A3, B3, Control);
  FULL_ADDER full_adder_1 (.A(Control), .B(A0), .C(xor_1_out), .Sum(out_10), .Carry(full_adder_1_carry));
  FULL_ADDER full_adder_2 (.A(full_adder_1_carry), .B(A1), .C(xor_2_out), .Sum(out_11), .Carry(full_adder_2_carry));
  FULL_ADDER full_adder_3 (.A(full_adder_2_carry), .B(A2), .C(xor_3_out), .Sum(out_12), .Carry(full_adder_3_carry));
  FULL_ADDER full_adder_4 (.A(full_adder_3_carry), .B(A3), .C(A3), .Sum(out_13), .Carry(out_14));
endmodule
