// Logisim project 4bitmemoryusingdflipflop.circ as structural Verilog: 1 circuit, main circuit main
module main (
  input  D0,
  input  D1,
  input  D2,
  input  D3,
  output Q0,
  output Q1,
  output Q2,
  output Q3
);

  wire CLK_out;

  Clock CLK (.out(CLK_out));
  D_Flip_Flop d_ff_1 (.D(D0), .clk(CLK_out), .Q(Q0));  // open: Qn, preset, reset
  D_Flip_Flop d_ff_2 (.D(D1), .clk(CLK_out), .Q(Q1));  // open: Qn, preset, reset
  D_Flip_Flop d_ff_3 (.D(D2), .clk(CLK_out), .Q(Q2));  // open: Qn, preset, reset
  D_Flip_Flop d_ff_4 (.D(D3), .clk(CLK_out), .Q(Q3));  // open: Qn, preset, reset

  // Notes on the sheet:
  //            4 BIT MEMORY USING D FLIP FLOP
endmodule
