// Logisim project 4bitshiftregister.circ as structural Verilog: 1 circuit, main circuit main
module main (
  input  serialdatainputs,
  input  shiftpulses,
  output out_3,
  output out_4
);

  wire d_ff_1_q, d_ff_2_q, d_ff_3_q;

  D_Flip_Flop d_ff_1 (.D(serialdatainputs), .clk(shiftpulses), .Q(d_ff_1_q));  // open: Qn, preset, reset
  D_Flip_Flop d_ff_2 (.D(d_ff_1_q), .clk(shiftpulses), .Q(d_ff_2_q));  // open: Qn, preset, reset
  D_Flip_Flop d_ff_3 (.D(d_ff_2_q), .clk(shiftpulses), .Q(d_ff_3_q));  // open: Qn, preset, reset
  D_Flip_Flop d_ff_4 (.D(d_ff_3_q), .clk(shiftpulses), .Q(out_3), .Qn(out_4));  // open: preset, reset

  // Notes on the sheet:
  //   4 bit shift register
endmodule
