// Logisim project frequencydividercircuitusinglogism.circ as structural Verilog: 1 circuit, main circuit main
module main (
  input  in_1,
  output out_2
);

  wire d_ff_1_qn;

  D_Flip_Flop d_ff_1 (.D(d_ff_1_qn), .clk(in_1), .Q(out_2), .Qn(d_ff_1_qn));  // open: preset, reset

  // Notes on the sheet:
  //   input frequency
  //               FREQUENCY DIVIDER USING FLIPFLOP
  //   feed back loop
  //   outp[ut frequency
endmodule
