// Logisim project masterslavedflipflop.circ as structural Verilog: 1 circuit, main circuit main
module main (
  input  D,
  output out_2
);

  wire CLK_out, d_ff_1_q, not_1_out;

  Clock CLK (.out(CLK_out));
  D_Flip_Flop d_ff_1 (.D(D), .clk(CLK_out), .Q(d_ff_1_q));  // open: Qn, preset, reset
  not not_1 (not_1_out, CLK_out);
  D_Flip_Flop d_ff_2 (.D(d_ff_1_q), .clk(not_1_out), .Q(out_2));  // open: Qn, preset, reset

  // Notes on the sheet:
  //   MASTER SLAVE D FLIPFLOP
endmodule
