// Logisim project dldlab4.circ as structural Verilog
module Assignment (
  input  A,
  input  B,
  input  C,
  input  A_2,
  input  B_2,
  input  C_2,
  output Output,
  output Output_2
);

  wire and_1_out, and_2_out, and_3_out, and_4_out, or_1_out;

  or or_1 (or_1_out, B, C);
  and and_1 (and_1_out, A, B);
  and and_2 (and_2_out, A, or_1_out);
  and and_3 (and_3_out, or_1_out, B);
  or or_2 (Output, and_1_out, and_2_out, and_3_out);
  and and_4 (and_4_out, A_2, C_2);
  or or_3 (Output_2, B_2, and_4_out);

  // Notes on the sheet:
  //   5 Gates
  //   2 Gates
endmodule

module ass (
  input  a,
  input  b,
  input  c,
  input  d,
  output e,
  output f,
  output g,
  output h,
  output i,
  output j,
  output k
);

  wire and_1_out, and_2_out, and_3_out, and_4_out, and_5_out, and_6_out, and_7_out, and_8_out, and_9_out,
       and_10_out, and_11_out, and_12_out, and_13_out, and_14_out, and_15_out, and_16_out, not_1_out,
       not_2_out, not_3_out, not_4_out, not_5_out, not_6_out, not_7_out, not_8_out, not_9_out, not_10_out,
       not_11_out, not_12_out, not_13_out, not_14_out, not_15_out, not_16_out, not_17_out, not_18_out,
       not_19_out, not_20_out, not_21_out, not_22_out, not_23_out, not_24_out, not_25_out;

  not not_1 (not_1_out, b);
  and and_1 (and_1_out, not_1_out, not_2_out);
  not not_2 (not_2_out, d);
  and and_2 (and_2_out, b, d);
  not not_3 (not_3_out, b);
  not not_4 (not_4_out, c);
  and and_3 (and_3_out, not_4_out, not_5_out);
  not not_5 (not_5_out, d);
  and and_4 (and_4_out, c, d);
  not not_6 (not_6_out, c);
  not not_7 (not_7_out, b);
  and and_5 (and_5_out, not_7_out, not_8_out);
  not not_8 (not_8_out, d);
  not not_9 (not_9_out, b);
  and and_6 (and_6_out, not_9_out, c);
  and and_7 (and_7_out, c, not_10_out);
  not not_10 (not_10_out, d);
  not not_11 (not_11_out, c);
  and and_8 (and_8_out, b, not_11_out, d);
  not not_12 (not_12_out, a);
  and and_9 (and_9_out, not_12_out, not_13_out, not_14_out);
  not not_13 (not_13_out, b);
  not not_14 (not_14_out, d);
  not not_15 (not_15_out, b);
  not not_16 (not_16_out, c);
  and and_10 (and_10_out, not_15_out, not_16_out, not_17_out);
  not not_17 (not_17_out, d);
  and and_11 (and_11_out, b, c, not_18_out);
  not not_18 (not_18_out, d);
  not not_19 (not_19_out, c);
  and and_12 (and_12_out, not_19_out, not_20_out);
  not not_20 (not_20_out, d);
  and and_13 (and_13_out, b, not_21_out);
  not not_21 (not_21_out, c);
  and and_14 (and_14_out, b, not_22_out);
  not not_22 (not_22_out, d);
  not not_23 (not_23_out, d);
  not not_24 (not_24_out, b);
  and and_15 (and_15_out, not_24_out, c);
  and and_16 (and_16_out, b, not_25_out);
  not not_25 (not_25_out, c);
  or or_1 (e, and_1_out, c, and_2_out, a);
  or or_2 (f, not_3_out, and_3_out, and_4_out, a);
  or or_3 (g, not_6_out, d, b, a);
  or or_4 (h, and_5_out, and_6_out, and_7_out, and_8_out, a);
  or or_5 (i, and_9_out, and_10_out, and_11_out);
  or or_6 (j, and_12_out, and_13_out, and_14_out, a);
  or or_7 (k, not_23_out, and_15_out, and_16_out, a);
endmodule

module ass2 (
  input  [3:0] in_1
);

  wire ass_1_e, ass_1_f, ass_1_g, ass_1_h, ass_1_i, ass_1_j, ass_1_k;

  ass ass_1 (
    .a(in_1[3]), .b(in_1[2]), .c(in_1[1]), .d(in_1[0]), .e(ass_1_e), .f(ass_1_f), .g(ass_1_g), .h(ass_1_h),
    .i(ass_1_i), .j(ass_1_j), .k(ass_1_k));
  _7_Segment_Display u_7_segment_display_1 (
    .g(ass_1_k), .f(ass_1_j), .a(ass_1_e), .b(ass_1_f), .e(ass_1_i), .d(ass_1_h), .c(ass_1_g));  // open: dp

  // Notes on the sheet:
  //   e
  //   f
  //   g
  //   h
  //   j
  //   i
  //   k
endmodule

module ass3 (
  input  A,
  input  B,
  input  C,
  input  D,
  output a_2,
  output b_2,
  output c_2,
  output d_2,
  output e,
  output f,
  output g
);

  wire and_1_out, and_2_out, and_3_out, and_4_out, and_5_out, and_6_out, and_7_out, and_8_out, and_9_out,
       and_10_out, and_11_out, and_12_out, and_13_out, and_14_out, and_15_out, and_16_out, and_17_out,
       and_18_out, and_19_out, and_20_out, and_21_out, and_22_out, and_23_out, and_24_out, and_25_out,
       and_26_out, and_27_out, and_28_out, and_29_out, and_30_out, and_31_out, and_32_out, and_33_out,
       and_34_out, and_35_out, not_1_out, not_2_out, not_3_out, not_4_out, not_5_out, not_6_out, not_7_out,
       not_8_out, not_9_out, not_10_out, not_11_out, not_12_out, not_13_out, not_14_out, not_15_out,
       not_16_out, not_17_out, not_18_out, not_19_out, not_20_out, not_21_out, not_22_out, not_23_out,
       not_24_out, not_25_out, not_26_out, not_27_out, not_28_out, not_29_out, not_30_out, not_31_out,
       not_32_out, not_33_out, not_34_out, not_35_out, not_36_out, not_37_out, not_38_out, not_39_out,
       not_40_out, not_41_out, not_42_out, not_43_out;

  not not_1 (not_1_out, B);
  and and_1 (and_1_out, not_1_out, not_2_out);
  not not_2 (not_2_out, D);
  not not_3 (not_3_out, A);
  and and_2 (and_2_out, not_3_out, C);
  not not_4 (not_4_out, A);
  and and_3 (and_3_out, not_4_out, B, D);
  and and_4 (and_4_out, B, C);
  and and_5 (and_5_out, A, not_5_out, not_6_out);
  not not_5 (not_5_out, B);
  not not_6 (not_6_out, C);
  and and_6 (and_6_out, A, not_7_out);
  not not_7 (not_7_out, D);
  not not_8 (not_8_out, A);
  and and_7 (and_7_out, not_8_out, not_9_out);
  not not_9 (not_9_out, B);
  not not_10 (not_10_out, A);
  and and_8 (and_8_out, not_10_out, not_11_out, not_12_out);
  not not_11 (not_11_out, C);
  not not_12 (not_12_out, D);
  not not_13 (not_13_out, B);
  and and_9 (and_9_out, not_13_out, not_14_out);
  not not_14 (not_14_out, D);
  not not_15 (not_15_out, A);
  and and_10 (and_10_out, not_15_out, C, D);
  and and_11 (and_11_out, A, not_16_out, D);
  not not_16 (not_16_out, C);
  not not_17 (not_17_out, A);
  and and_12 (and_12_out, not_17_out, not_18_out);
  not not_18 (not_18_out, C);
  not not_19 (not_19_out, A);
  and and_13 (and_13_out, not_19_out, D);
  not not_20 (not_20_out, C);
  and and_14 (and_14_out, not_20_out, D);
  not not_21 (not_21_out, A);
  and and_15 (and_15_out, not_21_out, B);
  and and_16 (and_16_out, A, not_22_out);
  not not_22 (not_22_out, B);
  not not_23 (not_23_out, A);
  not not_24 (not_24_out, B);
  and and_17 (and_17_out, not_23_out, not_24_out, not_25_out);
  not not_25 (not_25_out, D);
  not not_26 (not_26_out, C);
  and and_18 (and_18_out, B, not_26_out, D);
  and and_19 (and_19_out, B, C, not_27_out);
  not not_27 (not_27_out, D);
  and and_20 (and_20_out, A, not_28_out);
  not not_28 (not_28_out, C);
  and and_21 (and_21_out, A, not_29_out, D);
  not not_29 (not_29_out, B);
  not not_30 (not_30_out, B);
  and and_22 (and_22_out, not_30_out, not_31_out);
  not not_31 (not_31_out, D);
  and and_23 (and_23_out, C, not_32_out);
  not not_32 (not_32_out, D);
  and and_24 (and_24_out, A, C);
  and and_25 (and_25_out, A, B);
  not not_33 (not_33_out, C);
  and and_26 (and_26_out, not_33_out, not_34_out);
  not not_34 (not_34_out, D);
  not not_35 (not_35_out, A);
  and and_27 (and_27_out, not_35_out, B, not_36_out);
  not not_36 (not_36_out, C);
  and and_28 (and_28_out, B, not_37_out);
  not not_37 (not_37_out, D);
  and and_29 (and_29_out, A, not_38_out);
  not not_38 (not_38_out, B);
  and and_30 (and_30_out, A, C);
  not not_39 (not_39_out, B);
  and and_31 (and_31_out, not_39_out, C);
  and and_32 (and_32_out, C, not_40_out);
  not not_40 (not_40_out, D);
  not not_41 (not_41_out, A);
  and and_33 (and_33_out, not_41_out, B, not_42_out);
  not not_42 (not_42_out, C);
  and and_34 (and_34_out, A, not_43_out);
  not not_43 (not_43_out, B);
  and and_35 (and_35_out, A, D);
  or or_1 (b_2, and_7_out, and_8_out, and_9_out, and_10_out, and_11_out);
  or or_2 (c_2, and_12_out, and_13_out, and_14_out, and_15_out, and_16_out);
  or or_3 (d_2, and_17_out, and_18_out, and_19_out, and_20_out, and_21_out);
  or or_4 (e, and_22_out, and_23_out, and_24_out, and_25_out);
  or or_5 (f, and_26_out, and_27_out, and_28_out, and_29_out, and_30_out);
  or or_6 (g, and_31_out, and_32_out, and_33_out, and_34_out, and_35_out);
  or or_7 (a_2, and_1_out, and_2_out, and_3_out, and_4_out, and_5_out, and_6_out);
endmodule

module ass4 (
  input  [3:0] in_1
);

  wire ass3_1_a_2, ass3_1_b_2, ass3_1_c_2, ass3_1_d_2, ass3_1_e, ass3_1_f, ass3_1_g;

  ass3 ass3_1 (
    .A(in_1[3]), .B(in_1[2]), .C(in_1[1]), .D(in_1[0]), .a_2(ass3_1_a_2), .b_2(ass3_1_b_2), .c_2(ass3_1_c_2),
    .d_2(ass3_1_d_2), .e(ass3_1_e), .f(ass3_1_f), .g(ass3_1_g));
  _7_Segment_Display u_7_segment_display_1 (
    .g(ass3_1_g), .f(ass3_1_f), .a(ass3_1_a_2), .b(ass3_1_b_2), .e(ass3_1_e), .d(ass3_1_d_2), .c(ass3_1_c_2));  // open: dp
endmodule
