// Logisim project dld7.circ as structural Verilog
module A_B (
  input  in_1,
  input  B,
  input  A,
  input  in_4,
  output out_5
);

  Multiplexer multiplexer_1 (.in0(in_1), .in1(B), .out(out_5), .sel(A), .en(in_4));
endmodule

module A_B_2 (
  input  B,
  input  in_2,
  input  A,
  input  in_4,
  output out_5
);

  Multiplexer multiplexer_1 (.in0(B), .in1(in_2), .out(out_5), .sel(A), .en(in_4));
endmodule

module A_B_2_2 (
  input  B,
  input  in_2,
  input  A,
  input  in_4,
  output out_5
);

  Multiplexer multiplexer_1 (.in0(B), .in1(in_2), .out(out_5), .sel(A), .en(in_4));
endmodule

module A__B (
  input  in_1,
  input  B,
  input  A,
  input  in_4,
  output out_5
);

  Multiplexer multiplexer_1 (.in0(in_1), .in1(B), .out(out_5), .sel(A), .en(in_4));
endmodule

module _2_input_MUX (
  input  A,
  input  B,
  input  S,
  input  ENABLE,
  output out_5
);

  Multiplexer multiplexer_1 (.in0(A), .in1(B), .out(out_5), .sel(S), .en(ENABLE));
endmodule

module _4_input_MUX (
  input  A,
  input  B,
  input  C,
  input  D,
  input  enabler,
  input  S0,
  input  S1,
  output out_8
);

  Multiplexer #(.select(2)) multiplexer_1 (
    .in0(A), .in1(B), .in2(C), .in3(D), .out(out_8), .sel({S1, S0}), .en(enabler));
endmodule

module _1_bit_ALU (
  input  in_1,
  input  in_2,
  input  in_3,
  input  F2,
  input  in_5,
  input  F1,
  input  F0,
  input  C,
  input  in_9,
  input  B,
  input  A,
  output Y1,
  output Y0
);

  wire multiplexer_1_out, multiplexer_2_out, multiplexer_3_out, multiplexer_4_out, xor_1_out, xor_2_out;

  Multiplexer multiplexer_1 (.in0(in_2), .in1(B), .out(multiplexer_1_out), .sel(A));  // open: en
  Multiplexer multiplexer_2 (.in0(B), .in1(in_9), .out(multiplexer_2_out), .sel(A));  // open: en
  Multiplexer multiplexer_3 (.in0(B), .in1(in_5), .out(multiplexer_3_out), .sel(A));  // open: en
  xor xor_1 (xor_1_out, A, B);
  Multiplexer multiplexer_4 (.in0(in_3), .in1(B), .out(multiplexer_4_out), .sel(A));  // open: en
  xor xor_2 (xor_2_out, xor_1_out, C);
  Multiplexer #(.select(3)) multiplexer_5 (
    .in0(multiplexer_1_out), .in1(multiplexer_1_out), .in2(multiplexer_2_out), .in3(multiplexer_2_out),
    .in4(multiplexer_1_out), .in5(multiplexer_3_out), .in6(multiplexer_2_out), .in7(multiplexer_4_out),
    .out(Y1), .sel({C, F0, F1}));  // open: en
  Multiplexer #(.select(3)) multiplexer_6 (
    .in0(in_1), .in1(multiplexer_3_out), .in2(multiplexer_1_out), .in3(xor_1_out), .in4(xor_1_out),
    .in5(xor_1_out), .in6(xor_2_out), .in7(xor_2_out), .out(Y0), .sel({F2, F1, F0}));  // open: en
endmodule

module full_adder (
  input  in_1,
  input  in_2,
  input  C,
  input  A,
  input  B,
  output CARRY,
  output SUM
);

  wire not_1_out, not_2_out;

  not not_1 (not_1_out, C);
  not not_2 (not_2_out, C);
  Multiplexer #(.select(2)) multiplexer_1 (
    .in0(C), .in1(not_1_out), .in2(not_2_out), .in3(C), .out(SUM), .sel({A, B}));  // open: en
  Multiplexer #(.select(2)) multiplexer_2 (
    .in0(in_1), .in1(C), .in2(C), .in3(in_2), .out(CARRY), .sel({A, B}));  // open: en
endmodule
