// Logisim project dldlab5.circ as structural Verilog
module bin_to_gray (
  input  B3,
  input  B2,
  input  B1,
  input  B0,
  output G3,
  output G2,
  output G1,
  output G2_2
);

  xor xor_1 (G2, B3, B2);
  xor xor_2 (G1, B2, B1);
  xor xor_3 (G2_2, B1, B0);

  assign G3 = B3;

  // Notes on the sheet:
  //   MSB
  //   LSB
  //   BINARY TO GRAY
endmodule

module gray_to_binary (
  input  G3,
  input  G2,
  input  G1,
  input  G0,
  output B3,
  output B2,
  output B1,
  output B0
);

  xor xor_1 (B2, G3, G2);
  xor xor_2 (B1, B2, G1);
  xor xor_3 (B0, B1, G0);

  assign B3 = G3;

  // Notes on the sheet:
  //   LSB
  //   MSB
  //   GRAY TO BINARY
endmodule

module _2_bit_multiplier (
  input  A,
  input  B,
  input  C,
  input  D,
  output E,
  output F,
  output G,
  output H
);

  wire and_2_out, and_3_out, and_4_out, and_5_out, and_6_out, and_7_out, not_1_out, not_2_out, not_3_out,
       not_4_out, not_5_out, not_6_out;

  and and_1 (E, A, B, C, D);
  and and_2 (and_2_out, A, not_1_out, C);
  not not_1 (not_1_out, B);
  and and_3 (and_3_out, A, C, not_2_out);
  not not_2 (not_2_out, D);
  not not_3 (not_3_out, A);
  and and_4 (and_4_out, not_3_out, B, C);
  and and_5 (and_5_out, B, C, not_4_out);
  not not_4 (not_4_out, D);
  not not_5 (not_5_out, B);
  and and_6 (and_6_out, A, not_5_out, D);
  not not_6 (not_6_out, C);
  and and_7 (and_7_out, A, not_6_out, D);
  and and_8 (H, B, D);
  or or_1 (F, and_2_out, and_3_out);
  or or_2 (G, and_4_out, and_5_out, and_6_out, and_7_out);
endmodule

module _2_bit_minimized (
  input  [1:0] in_1,
  input  [1:0] in_2,
  output [3:0] out_3
);

  wire and_2_out, and_4_out, half_adder_1_c;

  and and_1 (out_3[0], in_1[0], in_2[0]);
  and and_2 (and_2_out, in_2[0], in_1[1]);
  and and_3 (and_2_out, in_2[1], in_1[0]);
  and and_4 (and_4_out, in_2[1], in_1[1]);
  half_adder half_adder_1 (.A(and_2_out), .B(and_2_out), .C(half_adder_1_c), .D(out_3[1]));
  half_adder half_adder_2 (.A(half_adder_1_c), .B(and_4_out), .C(out_3[3]), .D(out_3[2]));
endmodule

module half_adder (
  input  A,
  input  B,
  output C,
  output D
);

  wire and_2_out, and_3_out, not_1_out, not_2_out;

  and and_1 (C, A, B);
  not not_1 (not_1_out, A);
  not not_2 (not_2_out, B);
  and and_2 (and_2_out, not_1_out, B);
  and and_3 (and_3_out, A, not_2_out);
  or or_1 (D, and_2_out, and_3_out);
endmodule
