// Logisim project experiment 2.circ as structural Verilog
module nor_using_nand (
  input  A,
  input  B,
  output C
);

  wire nand_1_out, nand_2_out, nand_3_out;

  nand nand_1 (nand_1_out, A, A);
  nand nand_2 (nand_2_out, B, B);
  nand nand_3 (nand_3_out, nand_1_out, nand_2_out);
  nand nand_4 (C, nand_3_out, nand_3_out);
endmodule

module xor_using_nand (
  input  A,
  input  B,
  output C
);

  wire nand_1_out, nand_2_out, nand_3_out, nand_4_out;

  nand nand_1 (nand_1_out, A, A);
  nand nand_2 (nand_2_out, B, B);
  nand nand_3 (nand_3_out, nand_1_out, B);
  nand nand_4 (nand_4_out, A, nand_2_out);
  nand nand_5 (C, nand_3_out, nand_4_out);
endmodule

module half_adder (
  input  A,
  input  B,
  output S,
  output C
);

  wire and_2_out, and_3_out, not_1_out, not_2_out;

  not not_1 (not_1_out, B);
  not not_2 (not_2_out, A);
  and and_1 (C, A, B);
  and and_2 (and_2_out, A, not_1_out);
  and and_3 (and_3_out, not_2_out, B);
  or or_1 (S, and_2_out, and_3_out);
endmodule

module full_adder (
  input  A,
  input  B,
  input  cin,
  output sum,
  output carry
);

  wire and_1_out, and_2_out, and_3_out, and_4_out, and_5_out, and_6_out, and_7_out, not_1_out, not_2_out,
       not_3_out, not_4_out, not_5_out, not_6_out;

  not not_1 (not_1_out, A);
  not not_2 (not_2_out, B);
  not not_3 (not_3_out, A);
  not not_4 (not_4_out, cin);
  not not_5 (not_5_out, B);
  not not_6 (not_6_out, cin);
  and and_1 (and_1_out, B, cin);
  and and_2 (and_2_out, A, cin);
  and and_3 (and_3_out, A, B);
  and and_4 (and_4_out, not_1_out, not_2_out, cin);
  and and_5 (and_5_out, not_3_out, B, not_4_out);
  and and_6 (and_6_out, A, not_5_out, not_6_out);
  and and_7 (and_7_out, A, B, cin);
  or or_1 (carry, and_1_out, and_2_out, and_3_out);
  or or_2 (sum, and_4_out, and_5_out, and_6_out, and_7_out);
endmodule

module full_subtracter (
  input  A,
  input  B,
  input  C,
  output difference,
  output borrow
);

  wire and_1_out, and_2_out, and_3_out, and_4_out, and_5_out, and_6_out, and_7_out, not_1_out, not_2_out,
       not_3_out, not_4_out, not_5_out, not_6_out, not_7_out, not_8_out;

  not not_1 (not_1_out, A);
  not not_2 (not_2_out, B);
  not not_3 (not_3_out, A);
  not not_4 (not_4_out, C);
  not not_5 (not_5_out, B);
  not not_6 (not_6_out, C);
  not not_7 (not_7_out, A);
  not not_8 (not_8_out, A);
  and and_1 (and_1_out, not_1_out, not_2_out, C);
  and and_2 (and_2_out, not_3_out, B, not_4_out);
  and and_3 (and_3_out, A, not_5_out, not_6_out);
  and and_4 (and_4_out, A, B, C);
  and and_5 (and_5_out, not_7_out, C);
  and and_6 (and_6_out, not_8_out, B);
  and and_7 (and_7_out, B, C);
  or or_1 (difference, and_1_out, and_2_out, and_3_out, and_4_out);
  or or_2 (borrow, and_5_out, and_6_out, and_7_out);
endmodule

module half_subtracter (
  input  A,
  input  B,
  output difference,
  output borrow
);

  wire and_1_out, and_2_out, not_1_out, not_2_out, not_3_out;

  not not_1 (not_1_out, A);
  not not_2 (not_2_out, B);
  not not_3 (not_3_out, A);
  and and_1 (and_1_out, not_1_out, B);
  and and_2 (and_2_out, A, not_2_out);
  and and_3 (borrow, not_3_out, B);
  or or_1 (difference, and_1_out, and_2_out);
endmodule
