// Logisim project 10234.circ as structural Verilog
module _12_3_10_5_15 (
  output Q3,
  output Q2,
  output Q1,
  output Q0
);

  wire CLOCK_out, not_1_out, not_2_out, or_1_out, or_2_out, or_3_out;

  Clock CLOCK (.out(CLOCK_out));
  or or_1 (or_1_out, not_2_out, not_1_out);
  T_Flip_Flop t_ff_1 (.clk(CLOCK_out), .T(or_1_out), .Q(Q3));  // open: Qn, preset, reset, en
  not not_1 (not_1_out, Q3);
  not not_2 (not_2_out, Q0);
  T_Flip_Flop t_ff_2 (.clk(CLOCK_out), .T(not_2_out), .Q(Q2));  // open: Qn, preset, reset, en
  or or_2 (or_2_out, Q2, Q3);
  T_Flip_Flop t_ff_3 (.clk(CLOCK_out), .T(or_2_out), .Q(Q1));  // open: Qn, preset, reset, en
  or or_3 (or_3_out, Q1, Q3);
  T_Flip_Flop t_ff_4 (.clk(CLOCK_out), .T(or_3_out), .Q(Q0));  // open: Qn, preset, reset, en

  // Notes on the sheet:
  //   T3
  //   PAPER CODE 2
  //   T2
  //   4 bit synchronous counter with sequence12-3-10-5-15
  //   T1
  //   Yash Gupta
  //   S20200010234
  //   T0
endmodule
